# Fritzing sketch ECG (saved by Fritzing 0.9.2b)
circuit board: 8.46667cm x 5.64444cm
breadboards: 1

parts:
  EXG1 = BioAmp ECG Pill
  Part1 = Arduino Nano (Rev3.0)
  JP3 = Header 1 [package=1x01_offset]
  JP5 = Header 1 [package=1x01_offset]
  JP6 = Header 1 [package=1x01_offset]
  J1 = Piezo Speaker

nets:
  N1: EXG1.1, JP3.1
  N2: EXG1.2, JP5.1
  N3: EXG1.3, JP6.1
  N4: EXG1.4, Part1.VIN
  N5: EXG1.5, Part1.RESET
  N6: EXG1.6, Part1.A1
  N7: Part1.GND, J1.pin1
  N8: Part1.D13/SCK, J1.pin2

notes:
  Electrode connection
  Red: Below Right hand
  Black: Left wrist
  Black: Right wrist

custom parts:
  BioAmp ECG Pill: BioAmp EXG Pill is a small, powerful Analog Front End (AFE) biopotential signal acquisition board that can be paired with any 5 V Micro Controller Unit (MCU) with an ADC. It is capable of recording publication-quality biopotential signals like ECG, EMG, EOG, and EEG, without the inclusion of any dedicated hardware or software filters. It’s small size allows easy integration into mobile and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
  Header 1: Header 1 Standard 1-pin 0.1 header. Use with straight break away headers (SKU : PRT-00116), right angle break away headers (PRT-00553), swiss pins (PRT-00743), machine pins (PRT-00117), and female headers (PRT-00115).
  Header 1: Header 1 Standard 1-pin 0.1 header. Use with straight break away headers (SKU : PRT-00116), right angle break away headers (PRT-00553), swiss pins (PRT-00743), machine pins (PRT-00117), and female headers (PRT-00115).
