# Fritzing sketch EMG-Bar-Graph (saved by Fritzing 0.9.2b)
breadboards: 1

parts:
  EXG1 = BioAmp ECG Pill
  Part1 = Arduino Nano (Rev3.0)
  LED1 = LED - 3mm [color="Red (633nm)" package="3 mm [THT]"]
  R1 = Resistor [tolerance=±5% resistance=220 package=THT]
  LED2 = LED - 3mm [color="Red (660nm)" package="3 mm [THT]"]
  LED3 = LED - 3mm [color="Yellow (574nm)" package="3 mm [THT]"]
  LED4 = LED - 3mm [color="Yellow (585nm)" package="3 mm [THT]"]
  LED5 = LED - 3mm [color="Yellow (592nm)" package="3 mm [THT]"]
  LED6 = LED - 3mm [color="Yellow (595nm)" package="3 mm [THT]"]
  LED7 = LED - 3mm [color="Green (560nm)" package="3 mm [THT]"]
  LED8 = LED - 3mm [color="Green (560nm)" package="3 mm [THT]"]
  LED9 = LED - 3mm [color="Green (570nm)" package="3 mm [THT]"]
  R2 = Resistor [tolerance=±5% resistance=220 package=THT]
  R3 = Resistor [tolerance=±5% resistance=220 package=THT]
  R4 = Resistor [tolerance=±5% resistance=220 package=THT]
  R5 = Resistor [tolerance=±5% resistance=220 package=THT]
  R6 = Resistor [tolerance=±5% resistance=220 package=THT]
  R7 = Resistor [tolerance=±5% resistance=220 package=THT]
  R8 = Resistor [tolerance=±5% resistance=220 package=THT]
  R9 = Resistor [tolerance=±5% resistance=220 package=THT]
  JP3 = Header 1 [package=1x01_offset]
  JP5 = Header 1 [package=1x01_offset]
  JP6 = Header 1 [package=1x01_offset]

nets:
  N1: EXG1.1, JP3.1
  N2: EXG1.2, JP5.1
  N3: EXG1.3, JP6.1
  N4: EXG1.4, Part1.VIN
  N5: EXG1.5, Part1.RESET
  N6: EXG1.6, Part1.A1
  N7: Part1.D3, LED1.cathode, LED1.anode, R1.Pin_0
  N8: Part1.D4, LED2.cathode, LED2.anode, R2.Pin_0
  N9: Part1.D5, LED3.cathode, LED3.anode, R3.Pin_0
  N10: Part1.D6, LED4.cathode, LED4.anode, R4.Pin_0
  N11: Part1.D7, LED5.cathode, LED5.anode, R5.Pin_0
  N12: Part1.D8, LED6.cathode, LED6.anode, R6.Pin_0
  N13: Part1.D9, LED7.cathode, LED7.anode, R7.Pin_0
  N14: Part1.D10, LED8.cathode, LED8.anode, R8.Pin_0
  N15: Part1.D11/MOSI, LED9.cathode, LED9.anode, R9.Pin_0
  N16: R1.Pin_1, R2.Pin_1, R3.Pin_1, R4.Pin_1, R5.Pin_1, R6.Pin_1, R7.Pin_1, R8.Pin_1, R9.Pin_1

custom parts:
  BioAmp ECG Pill: BioAmp EXG Pill is a small, powerful Analog Front End (AFE) biopotential signal acquisition board that can be paired with any 5 V Micro Controller Unit (MCU) with an ADC. It is capable of recording publication-quality biopotential signals like ECG, EMG, EOG, and EEG, without the inclusion of any dedicated hardware or software filters. It’s small size allows easy integration into mobile and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
  Header 1: Header 1 Standard 1-pin 0.1 header. Use with straight break away headers (SKU : PRT-00116), right angle break away headers (PRT-00553), swiss pins (PRT-00743), machine pins (PRT-00117), and female headers (PRT-00115).
  Header 1: Header 1 Standard 1-pin 0.1 header. Use with straight break away headers (SKU : PRT-00116), right angle break away headers (PRT-00553), swiss pins (PRT-00743), machine pins (PRT-00117), and female headers (PRT-00115).
